# Fritzing sketch schematic (saved by Fritzing 1.0.6)
perfboards: 1

parts:
  SPKR1 = Loudspeaker  # not connected
  S1 = Pushbutton [package="[THT]"]
  Part1 = Adafruit MAX98357A I2S 3W Class D Amplifier [part_number="Adafruit #3006"]
  U1 = LIPO-1000mAh [package=lipo-1000]
  A1 = Weewooday 1.5-4.2 to 5v stepup converter [package=THT]
  A2 = Esp32-c3 super mini
  S2 = SWITCH-DPDT [package=gpi-152-3013]
  A3 = Weewooday 1.5-4.2 to 5v stepup converter [package=THT]
  JP1 = Header 2 [package=jst-2-pth]
  U2 = LIPO-1000mAh [package=lipo-1000]

nets:
  N1: S1.Pin_1, S1.Pin_2
  N2: S1.Pin_3, S1.Pin_4, A2.Pin_12
  N3: Part1.DIN, A2.Pin_2
  N4: Part1.BCLK, A2.Pin_13
  N5: Part1.LRCLK, A2.Pin_1
  N6: U1.+, A1.pin1
  N7: U1.-, A2.Pin_15
  N8: A1.pin3, A2.Pin_16
  N9: S2.4, A3.pin1
  N10: A3.pin2, U2.-
  N11: JP1.1, U2.+

custom parts:
  Adafruit MAX98357A I2S 3W Class D Amplifier: Listen to this good news - we now have an all in one digital audio amp breakout board that works incredibly well with the Raspberry Pi! If you're looking for an easy and low cost way to get you digital sound files bumpin' then the MAX08357 I2S Amp Breakout is for you. It takes standard I2S digital audio input and, not only decodes it into analog, but also amplifies it directly into a speaker.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
  Weewooday 1.5-4.2 to 5v stepup converter: Weewooday 1.5-4.2 to 5v stepup converter.
  Esp32-c3 super mini: ESP32-C3 Development Board ESP32 SuperMini Development Board ESP32 Development Board WiFi Bluetooth.
